# Fritzing sketch circuit v1_0 (saved by Fritzing 0.9.3b)
breadboards: 1

parts:
  Raspberry_Pi_1 = Raspberry Pi 3 [part_number=RPI-3-V1.2]
  CHG1 = TP4056 [chip_label=TP4056 package="DIP (Dual Inline) [THT]"]
  BAT1 = 18650 battery holder [package=battery-18650-kit]
  CHG2 = TP4056 [chip_label=TP4056 package="DIP (Dual Inline) [THT]"]
  BAT2 = 18650 battery holder [package=battery-18650-kit]
  DC-DC = RioRand LM2596
  7_4v_mains = Header 2 [package=screwterminal-3.5mm-2_lock]
  POW_SW = SWITCH-DPDT [package=eg2211]
  RGB_LED = RGB LED (com. cathode, rgb) [package="5 mm [THT]"]
  PAN = Basic Servo
  TILT = Basic Servo
  BOUNCE = Basic Servo
  RCWL-0516_Microwave_Radar_Motion_Sensor1 = RCWL-0516 Microwave Radar Motion Sensor Module
  MOTION_SW = SWITCH-DPDT [package=eg2211]

nets:
  3V3: Raspberry_Pi_1.3v3, Raspberry_Pi_1.3V3, MOTION_SW.4
  GND: Raspberry_Pi_1.GND, CHG2.pin2, DC-DC.Pin_4, RGB_LED.common_cathode, RCWL-0516_Microwave_Radar_Motion_Sensor1.GND
  N1: Raspberry_Pi_1.GPIO21, PAN.pulse
  N2: Raspberry_Pi_1.GPIO20, TILT.pulse
  N3: Raspberry_Pi_1.GPIO16, BOUNCE.pulse
  N4: Raspberry_Pi_1.GPIO25, MOTION_SW.5
  N5: Raspberry_Pi_1.GPIO24, RGB_LED.red_anode
  N6: Raspberry_Pi_1.GPIO23, RGB_LED.green_anode
  N7: Raspberry_Pi_1.GPIO18, RGB_LED.blue_anode
  5V: Raspberry_Pi_1.5V, DC-DC.Pin_3, POW_SW.2, RCWL-0516_Microwave_Radar_Motion_Sensor1.VIN
  N8: CHG1.pin1, POW_SW.1
  N9: CHG1.pin2, CHG2.pin1
  N10: CHG1.pin3, CHG2.pin3, POW_SW.6
  N11: CHG1.pin4, BAT1.+
  N12: CHG1.pin5, BAT1.-
  GND_2: CHG1.pin6, CHG2.pin6, DC-DC.Pin_2, 7_4v_mains.1, PAN.gnd, TILT.gnd, BOUNCE.gnd
  N13: CHG2.pin4, BAT2.+
  N14: CHG2.pin5, BAT2.-
  VCC: DC-DC.Pin_1, POW_SW.5, PAN.vcc, TILT.vcc, BOUNCE.vcc
  N15: 7_4v_mains.2, POW_SW.4
  N16: RCWL-0516_Microwave_Radar_Motion_Sensor1.OUT, MOTION_SW.6

notes:
  V1.1 2019-06-19

custom parts:
  TP4056: A DIP stand-in part for whatever IC you want. With 6 pins on a 300mil dual inline package (DIP) footprint.
  18650 battery holder: 18650 Battery Holder
  RCWL-0516 Microwave Radar Motion Sensor Module: The RCWL-0516 is a microwave radar motion sensor module. Input voltage is 4V to 28V. The 3V3 pin is a power output.
